# Fritzing sketch SmartFan (saved by Fritzing 0.9.3b)
breadboards: 2

parts:
  U1 = ESP32S-HiLetgo [part_number=ESP32S-HiLetgo]
  J1 = Piezo Speaker
  C1 = Electrolytic Capacitor [capacitance=10μF package="0605 [SMD, electrolytic]"]  # not connected
  A1 = DHT22 module
  U2 = ESP8266 NodeMCU LoLin module
  M1 = ac light dimmer 3terminal
  S1 = Momentary Switch [package=ksa_sealed_tac_switch]
  M2 = AC-05-03
  M3 = DC Motor

nets:
  N1: U1.GPIO25, J1.pin2
  GND: U1.GND, J1.pin1, A1.-, U2.GND, M1.GND, S1.1, S1.2, M2.pin_4
  VIN: U1.VIN, A1.+, U2.Vin, M1.VCC, M2.pin_3
  N2: U1.GPIO4, A1.Out
  N3: U1.GPIO16, U2.D8, U2.TX
  N4: U1.GPIO17, U2.D6, U2.RX
  N5: U1.GPIO5, M1.Z-C
  N6: U1.GPIO18, M1.PWM
  N7: U2.D5, S1.3, S1.4
  N8: M1.OUT, M3.pin_1
  N9: M1.N, M2.pin_2, M3.pin_2
  N10: M1.IN, M2.pin_1

custom parts:
  ESP32S-HiLetgo: HiLetgo ESP-WROOM-32 ESP32 ESP-32S Development Board 2.4GHz Dual-Mode WiFi + Bluetooth Dual Cores Microcontroller The ESP32 integrated with Antenna switches, RF Balun, power amplifiers, low-noise amplifiers, filters, and management modules, and the entire solution occupies the least area of PCB. 2.4 GHz Wi-Fi plus Bluetooth dual-mode chip, with TSMC Ultra-low power consumption 40nm technology,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
  DHT22 module: DHT22 module. Pins VCC Data GND.
  ESP8266 NodeMCU LoLin module: ESP8266 based NodeMCU
  ac light dimmer 3terminal: ac light dimmer module 3 output terminals.
  AC-05-03: AC-DC 220V to 5V Step-Down Power Supply Module
